# Fritzing sketch stop (saved by Fritzing 0.6.2b)
breadboards: 1

parts:
  Arduino1 = Arduino
  R6 = Resistor [tolerance=±5% resistance=220 package=THT]
  R7 = Resistor [tolerance=±5% resistance=220 package=THT]
  LED1 = Red LED - 5mm [package="5 mm [THT]"]  # not connected
  LED2 = Red LED - 5mm [package="5 mm [THT]"]  # not connected
  LED3 = Red LED - 5mm [package="5 mm [THT]"]  # not connected
  LED4 = Red LED - 5mm [package="5 mm [THT]"]  # not connected
  LED5 = Red LED - 5mm [package="5 mm [THT]"]  # not connected
  LED6 = Red LED - 5mm [package="5 mm [THT]"]  # not connected
  LED7 = Red LED - 5mm [package="5 mm [THT]"]  # not connected
  LED8 = Red LED - 5mm [package="5 mm [THT]"]  # not connected
  S1 = Pushbutton [package="[THT]"]
  R9 = Resistor [tolerance=±5% resistance=470 package=THT]
  R10 = Resistor [tolerance=±5% resistance=220 package=THT]
  R11 = Resistor [tolerance=±5% resistance=220 package=THT]
  R12 = Resistor [tolerance=±5% resistance=220 package=THT]
  R13 = Resistor [tolerance=±5% resistance=220 package=THT]
  R14 = Resistor [tolerance=±5% resistance=220 package=THT]
  R15 = Resistor [tolerance=±5% resistance=220 package=THT]

nets:
  N1: Arduino1.D11, R10.Pin_0
  N2: Arduino1.D10, R11.Pin_0
  N3: Arduino1.D9, R12.Pin_0
  N4: Arduino1.D8, R6.Pin_0
  N5: Arduino1.D7, R7.Pin_0
  N6: Arduino1.D6, R13.Pin_0
  N7: Arduino1.D5, R14.Pin_0
  N8: Arduino1.D4, R15.Pin_0
  N9: Arduino1.D2, S1.Pin_1, S1.Pin_2, R9.Pin_0
  N10: Arduino1.+5V, S1.Pin_3, S1.Pin_4
  N11: Arduino1.GND, R9.Pin_1
