# Fritzing sketch demo (saved by Fritzing 0.6.2b)
breadboards: 1

parts:
  R1 = Resistor [tolerance=±5% resistance=220 package=THT]
  R2 = Resistor [tolerance=±5% resistance=220 package=THT]
  R3 = Resistor [tolerance=±5% resistance=220 package=THT]
  R4 = Resistor [tolerance=±5% resistance=220 package=THT]
  R5 = Resistor [tolerance=±5% resistance=220 package=THT]
  R6 = Resistor [tolerance=±5% resistance=220 package=THT]
  R7 = Resistor [tolerance=±5% resistance=220 package=THT]
  R8 = Resistor [tolerance=±5% resistance=220 package=THT]
  R9 = Trimmer Potentiometer [maximum_resistance=10kΩ package=THT]
  U1 = 74HC595 [package="DIP16 [THT]"]
  Arduino1 = Arduino
  LED1 = green LED - 5mm [package="5 mm [THT]"]
  LED2 = green LED - 5mm [package="5 mm [THT]"]
  LED3 = green LED - 5mm [package="5 mm [THT]"]
  LED4 = green LED - 5mm [package="5 mm [THT]"]
  LED5 = green LED - 5mm [package="5 mm [THT]"]
  LED6 = green LED - 5mm [package="5 mm [THT]"]
  LED7 = green LED - 5mm [package="5 mm [THT]"]
  LED8 = green LED - 5mm [package="5 mm [THT]"]

nets:
  GND: R1.Pin_0, R2.Pin_0, R3.Pin_0, R4.Pin_0, R5.Pin_0, R6.Pin_0, R7.Pin_0, R8.Pin_0, R9.leg1, U1.GND, U1.OE, Arduino1.GND
  N1: R1.Pin_1, LED2.cathode
  N2: R2.Pin_1, LED3.cathode
  N3: R3.Pin_1, LED4.cathode
  N4: R4.Pin_1, LED5.cathode
  N5: R5.Pin_1, LED6.cathode
  N6: R6.Pin_1, LED7.cathode
  N7: R7.Pin_1, LED8.cathode
  N8: R8.Pin_1, LED1.cathode
  N9: R9.wiper, Arduino1.A0
  VCC: R9.leg2, U1.MR, U1.VCC, Arduino1.+5V
  N10: U1.Q1, LED8.anode
  N11: U1.Q2, LED7.anode
  N12: U1.Q3, LED6.anode
  N13: U1.Q4, LED5.anode
  N14: U1.Q5, LED4.anode
  N15: U1.Q6, LED3.anode
  N16: U1.Q7, LED2.anode
  N17: U1.SH_CP, Arduino1.D5
  N18: U1.ST_CP, Arduino1.D6
  N19: U1.DS, Arduino1.D7
  N20: U1.Q0, LED1.anode
