# Fritzing sketch double (saved by Fritzing 0.6.2b)
breadboards: 1

parts:
  U1 = 74HC595 [package="DIP16 [THT]"]
  U2 = 74HC595 [package="DIP16 [THT]"]
  J1 = screw terminal, 3 pins

nets:
  GND: U1.GND, U1.OE, U2.GND, U2.OE
  N1: U1.Q7', U2.DS
  5V: U1.MR, U1.VCC, U2.MR, U2.VCC
  N2: U1.SH_CP, U2.SH_CP, J1.pin3
  N3: U1.ST_CP, U2.ST_CP, J1.pin2
  N4: U1.DS, J1.pin1
